// Logisim project 231 INVALID.circ as structural Verilog: 1 circuit, main circuit main
module main (
  input  R1,
  input  P1,
  input  S1,
  input  R2,
  input  P2,
  input  S2,
  output out_7
);

  wire and_1_out, and_2_out, and_3_out, and_4_out, and_5_out, and_6_out, and_7_out, and_8_out, not_1_out,
       not_2_out, not_3_out, not_4_out, not_5_out, not_6_out, or_1_out, or_2_out, or_3_out;

  not not_1 (not_1_out, R1);
  not not_2 (not_2_out, P1);
  not not_3 (not_3_out, S1);
  not not_4 (not_4_out, R2);
  not not_5 (not_5_out, P2);
  not not_6 (not_6_out, S2);
  and and_1 (and_1_out, R1, P1);
  and and_2 (and_2_out, R1, S1);
  and and_3 (and_3_out, R2, P2);
  and and_4 (and_4_out, R2, S2);
  and and_5 (and_5_out, not_4_out, not_5_out, not_6_out);
  and and_6 (and_6_out, not_4_out, P2, S2);
  and and_7 (and_7_out, not_1_out, not_2_out, not_3_out);
  and and_8 (and_8_out, not_1_out, P1, S1);
  or or_1 (or_1_out, and_1_out, and_2_out, and_3_out);
  or or_2 (or_2_out, and_4_out, and_5_out, and_6_out);
  or or_3 (or_3_out, and_7_out, and_8_out);
  or or_4 (out_7, or_1_out, or_2_out, or_3_out);
endmodule
