// Logisim project 231 p1p2d.circ as structural Verilog: 1 circuit, main circuit main
module main (
  input  R1,
  input  P1,
  input  S1,
  input  R2,
  input  P2,
  input  S2,
  output P1_Wins,
  output P2_Wins,
  output Draw
);

  wire and_1_out, and_2_out, and_3_out, and_4_out, and_5_out, and_6_out, and_7_out, and_8_out, and_9_out,
       and_10_out, and_11_out, and_12_out, and_13_out, and_14_out, and_15_out, and_16_out, and_17_out,
       and_18_out, and_19_out, and_20_out, and_21_out, and_22_out, and_23_out, and_24_out, and_25_out,
       and_26_out, and_27_out, not_1_out, not_2_out, not_3_out, not_4_out, not_5_out, not_6_out;

  not not_1 (not_1_out, R1);
  not not_2 (not_2_out, P1);
  not not_3 (not_3_out, S1);
  not not_4 (not_4_out, R2);
  not not_5 (not_5_out, P2);
  not not_6 (not_6_out, S2);
  and and_1 (and_1_out, not_2_out, R1, not_3_out);
  and and_2 (and_2_out, not_5_out, R2, not_6_out);
  and and_3 (and_3_out, not_1_out, P1, not_3_out);
  and and_4 (and_4_out, not_4_out, P2, not_6_out);
  and and_5 (and_5_out, not_1_out, S1, not_5_out);
  and and_6 (and_6_out, not_4_out, S2, not_5_out);
  and and_7 (and_7_out, R1, not_2_out, not_3_out);
  and and_8 (and_8_out, not_4_out, not_5_out, S2);
  and and_9 (and_9_out, not_1_out, P1, not_3_out);
  and and_10 (and_10_out, R2, not_5_out, not_6_out);
  and and_11 (and_11_out, not_1_out, not_2_out, S1);
  and and_12 (and_12_out, not_4_out, P2, not_6_out);
  and and_13 (and_13_out, R1, not_2_out, not_3_out);
  and and_14 (and_14_out, not_4_out, P2, not_6_out);
  and and_15 (and_15_out, not_1_out, P1, not_3_out);
  and and_16 (and_16_out, not_4_out, not_5_out, S2);
  and and_17 (and_17_out, not_1_out, not_2_out, S1);
  and and_18 (and_18_out, R2, not_5_out, not_6_out);
  and and_19 (and_19_out, and_7_out, and_8_out);
  and and_20 (and_20_out, and_9_out, and_10_out);
  and and_21 (and_21_out, and_11_out, and_12_out);
  and and_22 (and_22_out, and_13_out, and_14_out);
  and and_23 (and_23_out, and_15_out, and_16_out);
  and and_24 (and_24_out, and_17_out, and_18_out);
  and and_25 (and_25_out, and_1_out, and_2_out);
  and and_26 (and_26_out, and_3_out, and_4_out);
  and and_27 (and_27_out, and_5_out, and_6_out);
  or or_1 (P1_Wins, and_19_out, and_20_out, and_21_out);
  or or_2 (P2_Wins, and_22_out, and_23_out, and_24_out);
  or or_3 (Draw, and_25_out, and_26_out, and_27_out);

  // Notes on the sheet:
  //   Rock-Paper-Scissor Game
endmodule
